# Fritzing sketch Unihack-arm-prosthetic (saved by Fritzing 0.9.3b)
breadboards: 1
stripboards: 2

parts:
  DC-DC_stepdown_3A_5V = RioRand LM2596
  DC-DC_stepdown_3A_6V = RioRand LM2596
  Raspberry_Pi1 = Raspberry Pi B+
  PWM1 = PCA9685 16x12-bit PWM Breakout
  Condensator_16V_470uF = Electrolytic Capacitor [capacitance=100µF voltage=16V package="200 mil [THT, electrolytic]"]
  DC1 = DC_DC_XL4016 [chip_label=XL4016 package=board_screw]  # not connected
  DC-DC_stepdown_8A_5_5v = DC_DC_XL4016 [package=board_screw]
  12V_battery = 12 battery [package=battery]  # not connected
  Power_plug1 = USB-C plug
  J1 = Basic Servo  # not connected

nets:
  N1: DC-DC_stepdown_3A_5V.Pin_1, DC-DC_stepdown_3A_6V.Pin_1, DC-DC_stepdown_8A_5_5v.IN+
  N2: DC-DC_stepdown_3A_5V.Pin_2, DC-DC_stepdown_3A_6V.Pin_2, DC-DC_stepdown_8A_5_5v.IN-
  N3: DC-DC_stepdown_3A_5V.Pin_3, Power_plug1.VCC
  N4: DC-DC_stepdown_3A_5V.Pin_4, Power_plug1.GND
  N5: Raspberry_Pi1.GND, PWM1.no_name_yet#501, Condensator_16V_470uF.-, DC-DC_stepdown_8A_5_5v.OUT-
  N6: PWM1.no_name_yet#506, Condensator_16V_470uF.+, DC-DC_stepdown_8A_5_5v.OUT+

custom parts:
  DC_DC_XL4016: DC-DC Converter step down voltage regulator XL4016 custom sketch.
  DC_DC_XL4016: DC-DC Converter step down voltage regulator XL4016 custom sketch.
  12 battery: 12V lead acid type battery, like the Husqvarna YTH2448 12V 35AH battery. This is the mini version 1/4 the size of the actual battery to be closer to typical breadboard parts (around 2in wide rathher than 7in). The pads in pcb are sized to accomidate up to 14ga wire (as these batterys will deliver high currents.)
  USB-C plug: power plug
